# Fritzing sketch attiny_breakout (saved by Fritzing 0.8.5b)
circuit board: 1.6cm x 2.8cm
breadboards: 1

parts:
  U1 = attiny85 [package=dip]
  R1 = Resistor [tolerance=±5% resistance=10k package=THT]
  D1 = Rectifier Diode [part_number=1N4001 package="300 mil [THT]"]
  J1 = male pin header, 4 pins [form="♂ (male)"]
  J2 = male pin header, 4 pins [form="♂ (male)"]
  SERIAL = male pin header, 6 pins [form="♂ (male)"]
  LOAD = male pin header, 2 pins [form="♂ (male)"]
  BC547 = NPN-Transistor [package="TO92 [THT]"]

nets:
  DATA: U1.Pin_1, D1.anode, J1.pin1, BC547.E
  N1: U1.Pin_2, J1.pin2, LOAD.pin2
  N2: U1.Pin_3, J1.pin3
  GND: U1.Pin_4, J1.pin4, SERIAL.pin1, LOAD.pin1
  N3: U1.Pin_5, J2.pin4
  N4: U1.Pin_6, J2.pin3
  N5: U1.Pin_7, J2.pin2
  N6: U1.Pin_8, J2.pin1
  TX: R1.Pin_0, D1.cathode, SERIAL.pin5
  N7: R1.Pin_1, BC547.B
  RX: SERIAL.pin4, BC547.C

notes:
  Microboard, ATtiny Breakout Board, 1A
  ATtiny
  GND
