# Fritzing sketch attiny_breakout_2 (saved by Fritzing 0.8.5b)
circuit board: 2cm x 4cm
breadboards: 1

parts:
  U1 = attiny85 [package=dip]
  R1 = Resistor [tolerance=±5% resistance=10k package=THT]
  D1 = Rectifier Diode [part_number=1N4001 package="300 mil [THT]"]
  J1 = male pin header, 4 pins [form="♂ (male)"]
  J2 = male pin header, 4 pins [form="♂ (male)"]
  SERIAL = male pin header, 6 pins [form="♂ (male)"]
  PWR = male pin header, 2 pins [form="♂ (male)"]
  BC547 = NPN-Transistor [package="TO92 [THT]"]
  DIP_SWITCH = DIP4 [package=DIL]

nets:
  DATA: U1.Pin_1, D1.anode, J1.pin1, BC547.E
  N1: U1.Pin_2, J1.pin2, DIP_SWITCH.3
  N2: U1.Pin_3, J1.pin3
  GND: U1.Pin_4, J1.pin4, SERIAL.pin1, DIP_SWITCH.2
  N3: U1.Pin_5, J2.pin4
  N4: U1.Pin_6, J2.pin3
  N5: U1.Pin_7, J2.pin2
  N6: U1.Pin_8, J2.pin1, DIP_SWITCH.4
  TX: R1.Pin_0, D1.cathode, SERIAL.pin5
  N7: R1.Pin_1, BC547.B
  VCC: SERIAL.pin3, PWR.pin1
  RX: SERIAL.pin4, BC547.C
  N8: PWR.pin2, DIP_SWITCH.1

notes:
  Microboard, ATtiny Breakout Board, 2A
  ATtiny
  GND
